# Fritzing sketch Fritzing_Schematic (saved by Fritzing 1.0.0d)

parts:
  Part1 = Arduino Uno (Rev3) - ICSP
  Mod1 = KY-008 Laser Transmitter Module [package="Breakout board"]
  Laser_Sensor_Module1 = Laser Sensor Module [part_number="Laser Sensor Module" chip_label=IC package="DIP (Dual Inline) [THT]"]

nets:
  N1: Part1.A0, Laser_Sensor_Module1.OUT
  N2: Part1.5V, Mod1.NC
  N3: Part1.GND, Mod1.-

notes:
  !! Check the pinout on the LASER module. Mine was backwards.!!
  <-- Out to Barn controller.

custom parts:
  KY-008 Laser Transmitter Module: KY-008 Laser Transmitter Module, emits a dot shaped red laser beam.
  Laser Sensor Module: Laser Sensor/Detector/Receiver Module Working Voltage: 5V
